// Logisim project Project1_circuit.circ as structural Verilog: 1 circuit, main circuit main
module main (
  input  A,
  input  B,
  input  in_3
);

  wire and_1_out, and_2_out, not_1_out, or_1_out;

  not not_1 (not_1_out, B);
  and and_1 (and_1_out, B, in_3);
  and and_2 (and_2_out, A, not_1_out);
  or or_1 (or_1_out, and_2_out, and_1_out);
  LED led_1 (.in(or_1_out));

  // Notes on the sheet:
  //   C
  //   F(A, B, C) = (AB') + (BC)
  //   B'
  //   BC
  //   AB'
  //   F(A, B, C) = AB' + BC
endmodule
